# Fritzing sketch digitalwk11 (saved by Fritzing 0.9.3b)
breadboards: 1

parts:
  元件1 = Arduino Uno (Rev3)
  LED1 = LED - 5mm [color="Red (633nm)" package="5 mm [THT]"]
  LED2 = LED - 5mm [color="Red (633nm)" package="5 mm [THT]"]
  R1 = Resistor [tolerance=±5% resistance=220 package=THT]
  R2 = Resistor [tolerance=±5% resistance=220 package=THT]

nets:
  N1: 元件1.D12/MISO, LED1.anode
  N2: 元件1.D13/SCK, LED2.anode
  N3: 元件1.GND, R1.Pin_0, R2.Pin_0
  N4: LED1.cathode, R2.Pin_1
  N5: LED2.cathode, R1.Pin_1
